# Fritzing sketch itp348_a4_xu_connie_fritzingfile (saved by Fritzing 0.9.10b)
breadboards: 1

parts:
  Argon1 = Particle Argon
  S1 = Pushbutton [package="[THT]"]
  R4 = Resistor [tolerance=±5% resistance=10k package="2512 [SMD]"]
  R3 = Resistor [tolerance=±5% resistance=220 package="2010 [SMD]"]
  R5 = Resistor [tolerance=±5% resistance=220 package="2010 [SMD]"]
  R6 = Resistor [tolerance=±5% resistance=220 package="2010 [SMD]"]
  R7 = Resistor [tolerance=±5% resistance=220 package="2010 [SMD]"]
  R8 = Resistor [tolerance=±5% resistance=220 package="2010 [SMD]"]
  R9 = Resistor [tolerance=±5% resistance=220 package="2010 [SMD]"]
  LED18 = smd LED [color="Red (633nm)" package="1206 [SMD]"]
  R10 = Resistor [tolerance=±5% resistance=220 package="2010 [SMD]"]
  R11 = Resistor [tolerance=±5% resistance=220 package="2010 [SMD]"]
  R12 = Resistor [tolerance=±5% resistance=220 package="2010 [SMD]"]
  LED19 = smd LED [color="Red (633nm)" package="1206 [SMD]"]
  LED20 = smd LED [color="Red (633nm)" package="1206 [SMD]"]
  LED21 = smd LED [color="Red (633nm)" package="1206 [SMD]"]
  LED22 = smd LED [color="Red (633nm)" package="1206 [SMD]"]
  LED23 = smd LED [color="Red (633nm)" package="1206 [SMD]"]
  LED24 = smd LED [color="Red (633nm)" package="1206 [SMD]"]
  LED25 = smd LED [color="Red (633nm)" package="1206 [SMD]"]
  LED26 = smd LED [color="Red (633nm)" package="1206 [SMD]"]

nets:
  N1: Argon1.3.3V, R4.Pin_0
  N2: Argon1.GND, S1.Pin_1, S1.Pin_2, R3.Pin_1, R5.Pin_1, R6.Pin_1, R7.Pin_1, R8.Pin_1, R9.Pin_1, R10.Pin_1, R11.Pin_1, R12.Pin_1
  N3: Argon1.A0, LED24.cathode
  N4: Argon1.A1, LED26.cathode
  N5: Argon1.A2, LED25.cathode
  N6: Argon1.D2, S1.Pin_3, S1.Pin_4, R4.Pin_1
  N7: Argon1.D3, LED18.cathode
  N8: Argon1.D4, LED19.cathode
  N9: Argon1.D5, LED20.cathode
  N10: Argon1.D6, LED21.cathode
  N11: Argon1.D7, LED22.cathode
  N12: Argon1.D8, LED23.cathode
  N13: R3.Pin_0, LED20.anode
  N14: R5.Pin_0, LED19.anode
  N15: R6.Pin_0, LED18.anode
  N16: R7.Pin_0, LED21.anode
  N17: R8.Pin_0, LED22.anode
  N18: R9.Pin_0, LED23.anode
  N19: R10.Pin_0, LED24.anode
  N20: R11.Pin_0, LED26.anode
  N21: R12.Pin_0, LED25.anode

custom parts:
  Particle Argon: The Argon is a powerful Wi-Fi enabled development board that can act as either a standalone Wi-Fi endpoint or Wi-Fi enabled gateway for Particle Mesh networks. It is based on the Nordic nRF52840 and has built-in battery charging circuitry so it’s easy to connect a Li-Po and deploy your local network in minutes. The Argon is great for connecting existing projects to the Particle Device Cloud or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
