# Fritzing sketch itp348_a5_xu_connie_fritzingfile (saved by Fritzing 0.9.10b)
breadboards: 1

parts:
  Argon1 = Particle Argon
  S1 = Momentary Switch [package=ksa_sealed_tac_switch]
  S2 = Momentary Switch [package=ksa_sealed_tac_switch]
  R1 = Resistor [tolerance=±5% resistance=10k package="0603 [SMD]"]
  R2 = Resistor [tolerance=±5% resistance=10k package="0603 [SMD]"]
  LED1 = RGB LED - (4 legs) [package="5 mm [THT]"]
  R4 = Resistor [tolerance=±5% resistance=330 package="0603 [SMD]"]
  R5 = Resistor [tolerance=±5% resistance=330 package="0603 [SMD]"]
  R6 = Resistor [tolerance=±5% resistance=330 package="0603 [SMD]"]

nets:
  N1: Argon1.3.3V, R1.Pin_0, R2.Pin_0
  N2: Argon1.GND, S1.2, S2.2, LED1.common_anode
  N3: Argon1.D2, S1.3
  N4: Argon1.D3, S2.3
  N5: Argon1.D4, R4.Pin_1
  N6: Argon1.D5, R5.Pin_1
  N7: Argon1.D6, R6.Pin_1
  N8: S1.4, R2.Pin_1
  N9: LED1.red_cathode, R4.Pin_0
  N10: LED1.green_cathode, R5.Pin_0
  N11: LED1.blue_cathode, R6.Pin_0

custom parts:
  Particle Argon: The Argon is a powerful Wi-Fi enabled development board that can act as either a standalone Wi-Fi endpoint or Wi-Fi enabled gateway for Particle Mesh networks. It is based on the Nordic nRF52840 and has built-in battery charging circuitry so it’s easy to connect a Li-Po and deploy your local network in minutes. The Argon is great for connecting existing projects to the Particle Device Cloud or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
