# Fritzing sketch itp348_a6_xu_connie_fritzingfile (saved by Fritzing 0.9.10b)
breadboards: 1

parts:
  Argon1 = Particle Argon
  Qwiic_OLED_Breakout1 = Qwiic_OLED_Breakout  # not connected
  DHT_1 = DHT20 Humidity and Temperature Sensor
  S1 = Pushbutton [package="[THT]"]
  R1 = Resistor [tolerance=±5% resistance=10k package="2512 [SMD]"]

nets:
  3.3V: Argon1.3.3V, DHT_1.VDD, R1.Pin_1
  N1: Argon1.A0, DHT_1.GND, S1.Pin_1, S1.Pin_2
  N2: Argon1.SDA, DHT_1.SDA
  N3: Argon1.SCL, DHT_1.SCL
  N4: Argon1.D2, S1.Pin_3, S1.Pin_4, R1.Pin_0

custom parts:
  Particle Argon: The Argon is a powerful Wi-Fi enabled development board that can act as either a standalone Wi-Fi endpoint or Wi-Fi enabled gateway for Particle Mesh networks. It is based on the Nordic nRF52840 and has built-in battery charging circuitry so it’s easy to connect a Li-Po and deploy your local network in minutes. The Argon is great for connecting existing projects to the Particle Device Cloud or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
  Qwiic_OLED_Breakout: The SparkFun Qwiic Micro OLED Breakout is a Qwiic-enabled version of our popular Micro OLED display! The small monochrome, blue-on-black OLED screen presents incredibly clear images for your viewing pleasure. It’s “micro,” but it still packs a punch --- the OLED display is crisp, and you can fit a deceivingly large amount of graphics on there. This breakout is perfect for adding graphics to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
