# Fritzing sketch itp348_a8_xu_connie_fritzingfile (saved by Fritzing 0.9.10b)
breadboards: 1

parts:
  Argon1 = Particle Argon
  J1 = Piezo Speaker
  S1 = Magnetic Door Switch [package=reed_switch_plastic]
  R1 = Resistor [tolerance=±5% power=0.25 resistance=10k package=THT]

nets:
  N1: Argon1.3.3V, R1.Pin_0
  N2: Argon1.GND, J1.pin1, S1.2
  N3: Argon1.D2, J1.pin2
  N4: Argon1.D3, S1.1, R1.Pin_1

custom parts:
  Particle Argon: The Argon is a powerful Wi-Fi enabled development board that can act as either a standalone Wi-Fi endpoint or Wi-Fi enabled gateway for Particle Mesh networks. It is based on the Nordic nRF52840 and has built-in battery charging circuitry so it’s easy to connect a Li-Po and deploy your local network in minutes. The Argon is great for connecting existing projects to the Particle Device Cloud or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
